# Fritzing sketch Schematics (saved by Fritzing 0.9.3b)

parts:
  Part1 = Bluetooth HC-05 Macho
  Mod1 = AD8232 HeartRate Monitor [part_number=SEN-12650]
  Part2 = Arduino Uno (Rev3)

nets:
  N1: Part1.TXD, Part2.D0/RX
  N2: Part1.RXD, Part2.D1/TX
  VCC: Part1.VCC, Part2.5V
  GND: Part1.GND, Mod1.GND, Part2.GND
  3.3V: Mod1.3.3v, Part2.3V3
  N3: Mod1.OUTPUT, Part2.A0
  N4: Mod1.LO-, Part2.D5_PWM
  N5: Mod1.LO+, Part2.D6_PWM

custom parts:
  AD8232 HeartRate Monitor: Sparkfun single lead heart rate monitor - Ad8232.
